# Fritzing sketch schema (saved by Fritzing 1.0.4)
breadboards: 1

parts:
  Part1 = Arduino Uno (Rev3)
  R1 = Resistor [tolerance=±5% resistance=220 power=0.25W package=THT]
  LED1 = LED - 5mm [color="Green (560nm)" current=0.030A package="5 mm [THT]"]
  T2 = Pushbutton [package="[THT]"]
  R2 = Resistor [tolerance=±5% resistance=10k power=0.25W package=THT]
  L3 = LED - 5mm [color="Green (560nm)" current=0.030A package="5 mm [THT]"]
  R3 = Resistor [tolerance=±5% resistance=220 power=0.25W package=THT]
  L1 = LED - 5mm [color="Green (560nm)" current=0.030A package="5 mm [THT]"]
  R4 = Resistor [tolerance=±5% resistance=220 power=0.25W package=THT]
  T1 = Pushbutton [package="[THT]"]
  R6 = Resistor [tolerance=±5% resistance=10k power=0.25W package=THT]
  LED_FLASH = LED - 5mm [color="Red (660nm)" current=0.030A package="5 mm [THT]"]
  R7 = Resistor [tolerance=±5% resistance=220 power=0.25W package=THT]
  POT = Rotary Potentiometer (Small) [maximum_resistance=100kΩ knob_status=50% power=0.5W package=THT]
  T3 = Pushbutton [package="[THT]"]
  L4 = LED - 5mm [color="Green (560nm)" current=0.030A package="5 mm [THT]"]
  R11 = Resistor [tolerance=±5% resistance=10k power=0.25W package=THT]
  R12 = Resistor [tolerance=±5% resistance=10k power=0.25W package=THT]
  T4 = Pushbutton [package="[THT]"]
  R13 = Resistor [tolerance=±5% resistance=220 power=0.25W package=THT]
  LCD2004-I2C1 = LCD2004-I2C

nets:
  N1: Part1.A0, POT.wiper
  N2: Part1.A4/SDA, LCD2004-I2C1.SDA
  N3: Part1.A5/SCL, LCD2004-I2C1.SCL
  N4: Part1.D9_PWM, R7.Pin_1
  N5: Part1.D10_PWM/SS, R3.Pin_1
  N6: Part1.D11_PWM/MOSI, R4.Pin_1
  N7: Part1.D12/MISO, R1.Pin_1
  N8: Part1.D13/SCK, R13.Pin_1
  N9: Part1.D2, T2.Pin_3, T2.Pin_4, R2.Pin_1
  N10: Part1.D3_PWM, T1.Pin_3, T1.Pin_4, R11.Pin_1
  N11: Part1.D4, R6.Pin_1, T3.Pin_3, T3.Pin_4
  N12: Part1.D5_PWM, R12.Pin_1, T4.Pin_3, T4.Pin_4
  5V: Part1.5V, T2.Pin_1, T2.Pin_2, T1.Pin_1, T1.Pin_2, POT.leg2, T3.Pin_1, T3.Pin_2, LCD2004-I2C1.VCC
  GND: Part1.GND, LED1.cathode, R2.Pin_0, L3.cathode, L1.cathode, R6.Pin_0, LED_FLASH.cathode, POT.leg1, L4.cathode, R11.Pin_0, R12.Pin_0, T4.Pin_1, T4.Pin_2, LCD2004-I2C1.GND
  N13: R1.Pin_0, L1.anode
  N14: LED1.anode, R3.Pin_0
  N15: L3.anode, R4.Pin_0
  N16: LED_FLASH.anode, R7.Pin_0
  N17: L4.anode, R13.Pin_0

custom parts:
  LCD2004-I2C: A standard character display with 4x20 characters. Comes in many colors with LCM2004 IIC attached.
